# Fritzing sketch 15khz-rgb-pattern-generator (saved by Fritzing 0.9.4)
breadboards: 1

parts:
  Composant1 = Arduino Nano (Rev3.0)
  S1 = SWITCH-MOMENTARY-2 [package=tactile-pth]

nets:
  GND: Composant1.GND, S1.1
  RED: Composant1.D2
  GREEN: Composant1.D3
  BLUE: Composant1.D4
  V.SYNC: Composant1.D5
  H.SYNC: Composant1.D6
  C.SYNC: Composant1.D7
  N1: Composant1.D8, S1.2

notes:
  C.SYNC
  GROUND
  BLUE
  GREEN
  RED
